# Fritzing sketch ESP32MQTT433BridgeDog v3 (saved by Fritzing 0.9.3b)

parts:
  433Tx2 = 433Mhz Transmitter - 3 pins [form="♂ (male)" package=THT]
  C2 = Electrolytic Capacitor [capacitance=0.1mF package="100 mil [THT, electrolytic]"]
  Touch_Sensors1 = Generic male header - 5 pins [form="♂ (male)" package=THT]
  DHT22_HEADER1 = DHT22 Header [form="♂ (male)" package=THT]
  ESPDEVKITV1_LHS1 = ESP32 DEVKITV1 LHS - 15 pins [form="♀ (female)" package=THT]
  ESPDEVKITV1_RHS1 = ESP32 DEVKITV1 RHS - 15 pins [form="♀ (female)" package=THT]
  J2 = female pin header, 3 pins [form="♀ (female)"]
  OLED_I2C1 = OLED I2C header [form="♂ (male)" package=THT]
  nrfL24L01+2 = nrf24l01+ [form="♂ (male)" package=THT]
  LED3 = smd LED [color="Red (635nm)" package="0603 [SMD]"]  # not connected
  LED4 = smd LED [color="Green (570nm)" package="0603 [SMD]"]  # not connected
  R6 = Resistor [tolerance=±5% resistance=4.7k package=THT]
  R7 = Resistor [tolerance=±5% resistance=4.7k package=THT]
  R8 = Resistor [tolerance=±5% resistance=330 package=THT]  # not connected
  DHT23 = Humidity and Temperature Sensor RHT03

nets:
  3.3V: 433Tx2.Vcc, C2.+, DHT22_HEADER1.+V, ESPDEVKITV1_RHS1.VDD_3V3, OLED_I2C1.Vcc, R6.Pin_0, R7.Pin_0
  GND: 433Tx2.GND, DHT22_HEADER1.0v, OLED_I2C1.GND
  GND_2: C2.-, ESPDEVKITV1_LHS1.GND, ESPDEVKITV1_RHS1.GND, nrfL24L01+2.GND
  N1: Touch_Sensors1.pin1zzz, ESPDEVKITV1_LHS1.GPIO13
  N2: Touch_Sensors1.pin2, ESPDEVKITV1_LHS1.GPIO12
  N3: Touch_Sensors1.pin3, ESPDEVKITV1_LHS1.GPIO14
  N4: Touch_Sensors1.pin4, ESPDEVKITV1_LHS1.GPIO27
  N5: DHT22_HEADER1.data, ESPDEVKITV1_LHS1.GPIO25
  5V: ESPDEVKITV1_LHS1.VIN, nrfL24L01+2.+5V
  N6: ESPDEVKITV1_RHS1.GPIO5, nrfL24L01+2.CE
  N7: ESPDEVKITV1_RHS1.GPIO18, nrfL24L01+2.SCK
  N8: ESPDEVKITV1_RHS1.GPIO19, nrfL24L01+2.MISO
  N9: ESPDEVKITV1_RHS1.GPIO21-I2C_SDA, OLED_I2C1.SDA
  N10: ESPDEVKITV1_RHS1.GPIO23, nrfL24L01+2.MOSI
  N11: J2.pin2, DHT23.Data-signal
  N12: J2.pin3, DHT23.Vcc

notes:
  Note that GPIO_NUM_34 – GPIO_NUM_39 are input mode only

custom parts:
  433Mhz Transmitter - 3 pins: 433Mhz Transmitter
  Generic male header - 5 pins: Generic male header
  OLED I2C header: Generic male header
  nrf24l01+: Generic male header
