# Fritzing sketch ESP32MQTT433BridgeDog v3_2 (saved by Fritzing 0.9.3b)
stripboards: 1

parts:
  C2 = Electrolytic Capacitor [capacitance=0.1mF package="100 mil [THT, electrolytic]"]
  Touch_Sensors1 = Generic male header - 5 pins [form="♂ (male)" package=THT]
  DHT22_HEADER1 = DHT22 Header [form="♂ (male)" package=THT]
  ESPDEVKITV1_LHS1 = ESP32 DEVKITV1 LHS - 15 pins [form="♀ (female)" package=THT]
  ESPDEVKITV1_RHS1 = ESP32 DEVKITV1 RHS - 15 pins [form="♀ (female)" package=THT]
  J2 = female pin header, 3 pins [form="♀ (female)"]
  OLED_I2C1 = OLED I2C header [form="♂ (male)" package=THT]
  nrfL24L01+2 = nrf24l01+ [form="♂ (male)" package=THT]
  LED3 = smd LED [color="Red (635nm)" package="0603 [SMD]"]  # not connected
  LED4 = smd LED [color="Green (570nm)" package="0603 [SMD]"]  # not connected
  R6 = Resistor [tolerance=±5% resistance=4.7k package=THT]
  R7 = Resistor [tolerance=±5% resistance=4.7k package=THT]
  R8 = Resistor [tolerance=±5% resistance=330 package=THT]
  DHT23 = Humidity and Temperature Sensor RHT03
  433Tx3 = 433Mhz Transmitter - 3 pins [form="♂ (male)" package=THT]
  J4 = LED male header [form="♂ (male)" package=THT]
  R9 = Resistor [tolerance=±5% resistance=330 package=THT]
  J5 = LED male header [form="♂ (male)" package=THT]

nets (from the schematic view):
  GND: C2.-, DHT22_HEADER1.0v, ESPDEVKITV1_LHS1.GND, ESPDEVKITV1_RHS1.GND, OLED_I2C1.GND, nrfL24L01+2.GND, 433Tx3.GND, J4.-Ve, J5.-Ve
  3.3V: C2.+, DHT22_HEADER1.+V, ESPDEVKITV1_RHS1.VDD_3V3, OLED_I2C1.Vcc, R6.Pin_0, R7.Pin_0, 433Tx3.Vcc
  N1: Touch_Sensors1.pin1zzz, ESPDEVKITV1_LHS1.GPIO13
  N2: Touch_Sensors1.pin2, ESPDEVKITV1_LHS1.GPIO12
  N3: Touch_Sensors1.pin3, ESPDEVKITV1_LHS1.GPIO14
  N4: Touch_Sensors1.pin4, ESPDEVKITV1_LHS1.GPIO27
  N5: Touch_Sensors1.pin5, ESPDEVKITV1_LHS1.GPIO32
  N6: DHT22_HEADER1.data, ESPDEVKITV1_LHS1.GPIO26
  5V: ESPDEVKITV1_LHS1.VIN, nrfL24L01+2.+5V
  N7: ESPDEVKITV1_LHS1.GPIO25, R8.Pin_0
  N8: ESPDEVKITV1_LHS1.GPIO33, 433Tx3.Data
  N9: ESPDEVKITV1_RHS1.GPIO4, nrfL24L01+2.CSN
  N10: ESPDEVKITV1_RHS1.GPIO5, nrfL24L01+2.CE
  N11: ESPDEVKITV1_RHS1.GPIO18, nrfL24L01+2.SCK
  N12: ESPDEVKITV1_RHS1.GPIO19, nrfL24L01+2.MISO
  N13: ESPDEVKITV1_RHS1.GPIO21-I2C_SDA, OLED_I2C1.SDA, R6.Pin_1
  N14: ESPDEVKITV1_RHS1.GPIO1, R9.Pin_0
  N15: ESPDEVKITV1_RHS1.GPIO22-I2C_SCL, OLED_I2C1.SCL, R7.Pin_1
  N16: ESPDEVKITV1_RHS1.GPIO23, nrfL24L01+2.MOSI
  N17: J2.pin1, DHT23.GND_2
  N18: J2.pin2, DHT23.Data-signal
  N19: J2.pin3, DHT23.Vcc
  N20: R8.Pin_1, J4.+Ve
  N21: R9.Pin_1, J5.+Ve

notes:
  Note that GPIO_NUM_34 – GPIO_NUM_39 are input mode only

custom parts:
  Generic male header - 5 pins: Generic male header
  OLED I2C header: Generic male header
  nrf24l01+: Generic male header
  433Mhz Transmitter - 3 pins: 433Mhz Transmitter
