# Fritzing sketch ESP32MQTT433BridgeDog (saved by Fritzing 0.9.3b)
stripboards: 1

parts:
  R2 = Resistor [tolerance=±5% resistance=330 package=THT]
  DHT22 = Humidity and Temperature Sensor RHT03
  ESPDEVKITV1_LHS = ESP32 DEVKITV1 LHS - 15 pins [form="♀ (female)" package=THT]
  ESPDEVKITV1_RHS = ESP32 DEVKITV1 RHS - 15 pins [form="♀ (female)" package=THT]
  LED1 = smd LED [color="Green (570nm)" package="0603 [SMD]"]
  LED2 = smd LED [color="Red (635nm)" package="0603 [SMD]"]  # not connected
  J1 = female pin header, 3 pins [form="♀ (female)"]
  OLED_I2C = OLED I2C header [form="♂ (male)" package=THT]
  nrfL24L01+1 = nrf24l01+ [form="♂ (male)" package=THT]
  433Tx1 = 433Mhz Transmitter - 3 pins [form="♂ (male)" package=THT]
  R4 = Resistor [tolerance=±5% resistance=4.7k package=THT]
  C1 = Electrolytic Capacitor [capacitance=0.1mF package="100 mil [THT, electrolytic]"]
  Touch_Sensors = Generic male header - 5 pins [form="♂ (male)" package=THT]
  R5 = Resistor [tolerance=±5% resistance=4.7k package=THT]
  DHT22_HEADER = DHT22 Header [form="♂ (male)" package=THT]

nets:
  N1: R2.Pin_0, ESPDEVKITV1_LHS.GPIO33
  N2: R2.Pin_1, LED1.anode
  N3: DHT22.Vcc, J1.pin3
  N4: DHT22.Data-signal, J1.pin2
  N5: DHT22.GND_2, J1.pin1
  5V: ESPDEVKITV1_LHS.VIN, nrfL24L01+1.+5V
  GND: ESPDEVKITV1_LHS.GND, ESPDEVKITV1_RHS.GND, nrfL24L01+1.GND, C1.-
  N6: ESPDEVKITV1_LHS.GPIO13, Touch_Sensors.pin1zzz
  N7: ESPDEVKITV1_LHS.GPIO12, Touch_Sensors.pin2
  N8: ESPDEVKITV1_LHS.GPIO14, Touch_Sensors.pin3
  N9: ESPDEVKITV1_LHS.GPIO27, Touch_Sensors.pin4
  N10: ESPDEVKITV1_LHS.GPIO25, DHT22_HEADER.data
  N11: ESPDEVKITV1_LHS.GPIO32, 433Tx1.data
  3.3V: ESPDEVKITV1_RHS.VDD_3V3, OLED_I2C.Vcc, 433Tx1.Vcc, R4.Pin_0, C1.+, R5.Pin_0, DHT22_HEADER.+V
  N12: ESPDEVKITV1_RHS.GPIO15, Touch_Sensors.pin5
  N13: ESPDEVKITV1_RHS.GPIO16, nrfL24L01+1.CSN
  N14: ESPDEVKITV1_RHS.GPIO5, nrfL24L01+1.CE
  N15: ESPDEVKITV1_RHS.GPIO18, nrfL24L01+1.SCK
  N16: ESPDEVKITV1_RHS.GPIO19, nrfL24L01+1.MISO
  N17: ESPDEVKITV1_RHS.GPIO21-I2C_SDA, OLED_I2C.SDA, R5.Pin_1
  N18: ESPDEVKITV1_RHS.GPIO22-I2C_SCL, OLED_I2C.SCL, R4.Pin_1
  N19: ESPDEVKITV1_RHS.GPIO23, nrfL24L01+1.MOSI
  GND_2: OLED_I2C.GND, 433Tx1.GND, DHT22_HEADER.0v

notes:
  DEVKIT V1
  row spacing 10 holes
  row1 to 11
  GPIO 25
  (DHT22)
  SDA GPIO 21
  SCL GPIO 22
  Note that GPIO_NUM_34 – GPIO_NUM_39 are input mode only

custom parts:
  OLED I2C header: Generic male header
  nrf24l01+: Generic male header
  433Mhz Transmitter - 3 pins: 433Mhz Transmitter
  Generic male header - 5 pins: Generic male header
