# Fritzing sketch Untitled Sketch 2 (saved by Fritzing 0.9.3b)
breadboards: 1

parts:
  ESP32_DO-IT_DEVKITV1 = IC, DIP package, 30 pins [chip_label="ESP32 DO-IT DEVKITV1"]

nets:
  N1: ESP32_DO-IT_DEVKITV1.pin1, ESP32_DO-IT_DEVKITV1.pin2, ESP32_DO-IT_DEVKITV1.pin3, ESP32_DO-IT_DEVKITV1.pin4, ESP32_DO-IT_DEVKITV1.pin5
  N2: ESP32_DO-IT_DEVKITV1.pin8, ESP32_DO-IT_DEVKITV1.pin9, ESP32_DO-IT_DEVKITV1.pin10, ESP32_DO-IT_DEVKITV1.pin11, ESP32_DO-IT_DEVKITV1.pin12
  N3: ESP32_DO-IT_DEVKITV1.pin15, ESP32_DO-IT_DEVKITV1.pin16
  N4: ESP32_DO-IT_DEVKITV1.pin19, ESP32_DO-IT_DEVKITV1.pin20, ESP32_DO-IT_DEVKITV1.pin21, ESP32_DO-IT_DEVKITV1.pin22, ESP32_DO-IT_DEVKITV1.pin23
  N5: ESP32_DO-IT_DEVKITV1.pin26, ESP32_DO-IT_DEVKITV1.pin27, ESP32_DO-IT_DEVKITV1.pin28, ESP32_DO-IT_DEVKITV1.pin29, ESP32_DO-IT_DEVKITV1.pin30
