# Fritzing sketch ESP32MQTT433BridgeDog v4_0_lightsensor_use (saved by Fritzing 0.9.3b)
stripboards: 1

parts:
  C2 = Electrolytic Capacitor [capacitance=0.1mF package="100 mil [THT, electrolytic]"]
  Touch_Sensors = Generic male header - 5 pins [form="♂ (male)" package=THT]
  ESPDEVKITV1_RHS1 = ESP32 DEVKITV1 RHS - 15 pins [form="♀ (female)" package=THT]
  J2 = female pin header, 3 pins [form="♀ (female)"]
  OLED_I2C_Header = OLED I2C header [form="♂ (male)" package=THT]
  nrfL24L01_Header = nrf24l01+ [form="♂ (male)" package=THT]
  LED3 = smd LED [color="Red (635nm)" package="0603 [SMD]"]  # not connected
  LED4 = smd LED [color="Green (555nm)" package="0603 [SMD]"]  # not connected
  R6 = Resistor [tolerance=±5% resistance=4.7k package=THT]
  R7 = Resistor [tolerance=±5% resistance=4.7k package=THT]
  R8 = Resistor [tolerance=±5% resistance=330 package=THT]
  DHT23 = Humidity and Temperature Sensor RHT03
  DHT22_Header = DHT22 Header [form="♂ (male)" package=THT]
  R9 = Resistor [tolerance=±5% resistance=220 package=THT]
  ESPDEVKITV1_LHS1 = ESP32 DEVKITV1 LHS - 15 pins [form="♀ (female)" package=THT]
  433_rx_f_header = 433Mhx Rx female header [form="♀ (female)" package=THT]
  C3 = Electrolytic Capacitor [capacitance=10µF package="100 mil [THT, electrolytic]"]
  LED_f_Header = female pin header, 2 pins [form="♀ (female)"]  # not connected
  RED_LED_Header = LED Female Header [form="♀ (female)" package=THT]
  Green_LED_Header = LED Female Header [form="♀ (female)" package=THT]
  J4 = female pin header, 3 pins [form="♀ (female)"]  # not connected
  433Mhx_Tx_Header = 433Mhz Tx Female Header [form="♀ (female)" package=THT]
  J5 = male pin header, 2 pins [form="♂ (male)"]  # not connected
  R10 = Photocell (LDR) [package=THT]  # not connected
  LDR_Header = single row smd female pin header, 2 pins [form="♀ (female)"]
  J3 = male pin header, 2 pins [form="♂ (male)"]  # not connected
  R11 = Resistor [tolerance=±5% resistance=220 package=THT]  # not connected

nets (from the schematic view):
  GND: C2.-, ESPDEVKITV1_RHS1.GND, OLED_I2C_Header.GND, nrfL24L01_Header.GND, DHT22_Header.0v, ESPDEVKITV1_LHS1.GND, 433_rx_f_header.GND, C3.-, RED_LED_Header.-ve, Green_LED_Header.-ve, 433Mhx_Tx_Header.GND
  3.3V: C2.+, ESPDEVKITV1_RHS1.VDD_3V3, OLED_I2C_Header.Vcc, R6.Pin_0, R7.Pin_0, DHT22_Header.+V, 433_rx_f_header.Vcc, 433Mhx_Tx_Header.Vcc
  N1: Touch_Sensors.pin1zzz, ESPDEVKITV1_LHS1.GPIO13
  N2: Touch_Sensors.pin2, ESPDEVKITV1_LHS1.GPIO12
  N3: Touch_Sensors.pin3, ESPDEVKITV1_LHS1.GPIO14
  N4: Touch_Sensors.pin4, ESPDEVKITV1_LHS1.GPIO27
  N5: Touch_Sensors.pin5, ESPDEVKITV1_RHS1.GPIO15
  N6: ESPDEVKITV1_RHS1.GPIO4, nrfL24L01_Header.CSN
  N7: ESPDEVKITV1_RHS1.GPIO5, nrfL24L01_Header.CE
  N8: ESPDEVKITV1_RHS1.GPIO18, nrfL24L01_Header.SCK
  N9: ESPDEVKITV1_RHS1.GPIO19, nrfL24L01_Header.MISO
  N10: ESPDEVKITV1_RHS1.GPIO21-I2C_SDA, OLED_I2C_Header.SDA, R6.Pin_1
  N11: ESPDEVKITV1_RHS1.GPIO3, LDR_Header.pin2
  N12: ESPDEVKITV1_RHS1.GPIO22-I2C_SCL, OLED_I2C_Header.SCL, R7.Pin_1
  N13: ESPDEVKITV1_RHS1.GPIO23, nrfL24L01_Header.MOSI
  N14: J2.pin1, DHT23.GND_2
  N15: J2.pin2, DHT23.Data-signal
  N16: J2.pin3, DHT23.Vcc
  5V: nrfL24L01_Header.+5V, ESPDEVKITV1_LHS1.VIN, C3.+
  N17: R8.Pin_0, ESPDEVKITV1_LHS1.GPIO33
  N18: R8.Pin_1, Green_LED_Header.+ve
  N19: DHT22_Header.data, ESPDEVKITV1_LHS1.GPIO25
  N20: R9.Pin_0, ESPDEVKITV1_LHS1.GPIO26
  N21: R9.Pin_1, RED_LED_Header.+ve
  N22: ESPDEVKITV1_LHS1.GPIO32, 433Mhx_Tx_Header.Data
  N23: ESPDEVKITV1_LHS1.GPIO35, 433_rx_f_header.DATA1

notes:
  Note that GPIO_NUM_34 – GPIO_NUM_39 are input mode only
  note orange wire for 5v tx vcc mod

custom parts:
  Generic male header - 5 pins: Generic male header
  OLED I2C header: Generic male header
  nrf24l01+: Generic male header
